// Digital circuit cpu.dig as structural Verilog
module cpu (
  input  in_1,
  input  in_2,
  input  in_3,
  input  in_4,
  input  in_5,
  input  in_6,
  input  in_7,
  input  clk
);

  wire adder_1_p10, adder_1_p11, adder_2_p10, adder_2_p11, adder_2_p12, adder_2_p13, and_1_out, and_2_out,
       and_3_out, and_4_out, and_5_out, and_6_out, button_1_out, button_2_out, counter_resetable_1_o_0,
       counter_resetable_1_o_1, counter_resetable_1_o_2, counter_resetable_1_o_3, counter_resetable_2_o_0,
       counter_resetable_2_o_1, counter_resetable_2_o_2, counter_resetable_2_o_3, curr_instr_in,
       decoder_6_to_64_1_p3, decoder_6_to_64_1_p4, decoder_6_to_64_1_p5, decoder_6_to_64_1_p6,
       decoder_6_to_64_1_p8, decoder_6_to_64_1_p9, decoder_6_to_64_1_p10, decoder_6_to_64_1_p11,
       decoder_6_to_64_1_p12, decoder_6_to_64_1_p13, decoder_6_to_64_1_p14, decoder_6_to_64_1_p15,
       decoder_6_to_64_1_p16, decoder_6_to_64_1_p17, decoder_6_to_64_1_p18, decoder_6_to_64_1_p19,
       delay_1_out, delay_2_out, delay_3_out, delay_4_out, delay_5_out, delay_6_out, halt, madr_in, madr_q_0,
       madr_q_1, madr_q_2, madr_q_3, mem_out, memory2_1_o_0, memory2_1_o_1, memory2_1_o_2, memory2_1_o_3,
       memory2_1_o_4, memory2_1_o_5, memory2_1_o_6, memory2_1_o_7, nor_1_out, not_1_out, not_2_out,
       not_3_out, not_4_out, not_5_out, not_6_out, not_7_out, not_8_out, or_1_out, pc_inc, pc_out, pc_reset,
       reg_A_in, register_simple_1_q_0, register_simple_1_q_1, register_simple_1_q_2, register_simple_1_q_3,
       register_simple_2_q_0, register_simple_2_q_1, register_simple_2_q_2, register_simple_2_q_3,
       tri_state_buffer_4bit_1_o_0, tri_state_buffer_4bit_1_o_1, tri_state_buffer_4bit_1_o_2,
       tri_state_buffer_4bit_1_o_3, tri_state_buffer_4bit_2_o_0, tri_state_buffer_4bit_2_o_1,
       tri_state_buffer_4bit_2_o_2, tri_state_buffer_4bit_2_o_3;
  wire [7:0] driver_6_out, driver_7_out;

  Delay #(.delayTime(20), .generic("this.Duration = args.duration;")) delay_1 (.in(button_1_out), .out(delay_1_out));
  Button #(.activeLow("true")) button_1 (.out(button_1_out));
  Button button_2 (.out(button_2_out));
  not not_1 (not_1_out, delay_1_out);
  or or_1 (or_1_out, halt, clk);
  and and_1 (and_1_out, button_1_out, not_1_out);
  or or_2 (pc_reset, and_1_out, in_7, button_2_out);
  not not_2 (not_2_out, pc_reset);
  not not_3 (not_3_out, or_1_out);
  not not_4 (not_4_out, pc_reset);
  and and_2 (and_2_out, not_2_out, not_3_out);
  and and_3 (and_3_out, not_4_out, or_1_out);
  Delay #(.delayTime(20)) delay_2 (.in(1'b1), .out(delay_2_out));
  Delay #(.delayTime(20)) delay_3 (.in(delay_2_out), .out(delay_3_out));
  Delay #(.delayTime(20)) delay_4 (.in(delay_3_out), .out(delay_4_out));
  Delay #(.delayTime(20)) delay_5 (.in(delay_4_out), .out(delay_5_out));
  Delay #(.delayTime(20)) delay_6 (.in(delay_5_out), .out(delay_6_out));
  counter_resetable counter_resetable_1 (
    .C(and_3_out), .R(and_6_out), .S(1'b0), .D_0(1'b0), .D_1(1'b0), .D_2(1'b0), .D_3(1'b0), .R_a(pc_reset),
    .O_0(counter_resetable_1_o_0), .O_1(counter_resetable_1_o_1), .O_2(counter_resetable_1_o_2),
    .O_3(counter_resetable_1_o_3));
  not not_5 (not_5_out, counter_resetable_1_o_0);
  not not_6 (not_6_out, counter_resetable_1_o_1);
  not not_7 (not_7_out, counter_resetable_1_o_2);
  not not_8 (not_8_out, counter_resetable_1_o_3);
  and and_4 (and_4_out, not_5_out, not_6_out, not_7_out, not_8_out);
  and and_5 (and_5_out, counter_resetable_1_o_0, not_6_out, not_7_out, not_8_out);
  and and_6 (and_6_out, counter_resetable_1_o_0, counter_resetable_1_o_2);
  // adder adder_1: pin names not known; wires that end beside it: 1'b0, 1'b0, 1'b1, 1'b0, 1'b0, counter_resetable_1_o_0, counter_resetable_1_o_1, counter_resetable_1_o_2, counter_resetable_1_o_3, adder_1_p10, adder_1_p11
  assign pc_out = and_4_out ? and_4_out : 1'bz;  // Driver driver_1
  assign madr_in = and_4_out ? and_4_out : 1'bz;  // Driver driver_2
  assign curr_instr_in = and_5_out ? and_5_out : 1'bz;  // Driver driver_3
  assign pc_inc = and_5_out ? and_5_out : 1'bz;  // Driver driver_4
  assign mem_out = and_5_out ? and_5_out : 1'bz;  // Driver driver_5
  nor nor_1 (nor_1_out, and_4_out, and_5_out);
  // decoder_6_to_64 decoder_6_to_64_1: pin names not known; wires that end beside it: adder_1_p10, adder_1_p11, decoder_6_to_64_1_p3, decoder_6_to_64_1_p4, decoder_6_to_64_1_p5, decoder_6_to_64_1_p6, nor_1_out, decoder_6_to_64_1_p8, decoder_6_to_64_1_p9, decoder_6_to_64_1_p10, decoder_6_to_64_1_p11, decoder_6_to_64_1_p12, decoder_6_to_64_1_p13, decoder_6_to_64_1_p14, decoder_6_to_64_1_p15, decoder_6_to_64_1_p16, decoder_6_to_64_1_p17, decoder_6_to_64_1_p18, decoder_6_to_64_1_p19, decoder_6_to_64_1_p12, decoder_6_to_64_1_p13, decoder_6_to_64_1_p14, decoder_6_to_64_1_p16, decoder_6_to_64_1_p17, decoder_6_to_64_1_p18
  assign {driver_6_out[7:5], halt, driver_6_out[3:0]} = decoder_6_to_64_1_p11 ? 8'h10 : 8'bz;  // Driver driver_6
  assign {driver_7_out[7:6], reg_A_in, driver_7_out[4:3], mem_out, driver_7_out[1:0]} = decoder_6_to_64_1_p15 ? 8'h24 : 8'bz;  // Driver driver_7
  register_simple madr (
    .E_out(madr_in), .CLK(and_2_out), .D_0(tri_state_buffer_4bit_1_o_0), .D_1(tri_state_buffer_4bit_1_o_1),
    .D_2(tri_state_buffer_4bit_1_o_2), .D_3(tri_state_buffer_4bit_1_o_3), .Q_0(madr_q_0), .Q_1(madr_q_1),
    .Q_2(madr_q_2), .Q_3(madr_q_3));
  PullDown pulldown_1 (.out(pc_inc));
  memory2 memory2_1 (
    .a_0(madr_q_0), .a_1(madr_q_1), .a_2(madr_q_2), .a_3(madr_q_3), .E(in_1), .C(and_2_out),
    .D_0(tri_state_buffer_4bit_1_o_0), .D_1(tri_state_buffer_4bit_1_o_1), .D_2(tri_state_buffer_4bit_1_o_2),
    .D_3(tri_state_buffer_4bit_1_o_3), .O_0(memory2_1_o_0), .O_1(memory2_1_o_1), .O_2(memory2_1_o_2),
    .O_3(memory2_1_o_3), .O_4(memory2_1_o_4), .O_5(memory2_1_o_5), .O_6(memory2_1_o_6), .O_7(memory2_1_o_7));
  PullDown pulldown_2 (.out(halt));
  PullDown pulldown_3 (.out(reg_A_in));
  PullDown pulldown_4 (.out(mem_out));
  PullDown pulldown_5 (.out(curr_instr_in));
  PullDown pulldown_6 (.out(madr_in));
  PullDown pulldown_7 (.out(pc_out));
  tri_state_buffer_4bit tri_state_buffer_4bit_1 (
    .D_0(memory2_1_o_0), .D_1(memory2_1_o_1), .D_2(memory2_1_o_2), .D_3(memory2_1_o_3), .E(mem_out),
    .O_0(tri_state_buffer_4bit_1_o_0), .O_1(tri_state_buffer_4bit_1_o_1), .O_2(tri_state_buffer_4bit_1_o_2),
    .O_3(tri_state_buffer_4bit_1_o_3));
  tri_state_buffer_4bit tri_state_buffer_4bit_2 (
    .D_0(memory2_1_o_4), .D_1(memory2_1_o_5), .D_2(memory2_1_o_6), .D_3(memory2_1_o_7), .E(mem_out),
    .O_0(tri_state_buffer_4bit_2_o_0), .O_1(tri_state_buffer_4bit_2_o_1), .O_2(tri_state_buffer_4bit_2_o_2),
    .O_3(tri_state_buffer_4bit_2_o_3));
  register_simple Current_Instruction_HI (
    .E_out(curr_instr_in), .CLK(and_2_out), .D_0(tri_state_buffer_4bit_2_o_0),
    .D_1(tri_state_buffer_4bit_2_o_1), .D_2(tri_state_buffer_4bit_2_o_2), .D_3(tri_state_buffer_4bit_2_o_3),
    .Q_0(decoder_6_to_64_1_p3), .Q_1(decoder_6_to_64_1_p4), .Q_2(decoder_6_to_64_1_p5),
    .Q_3(decoder_6_to_64_1_p6));
  register_simple Current_Instruction_LO (
    .E_out(curr_instr_in), .CLK(and_2_out), .D_0(tri_state_buffer_4bit_1_o_0),
    .D_1(tri_state_buffer_4bit_1_o_1), .D_2(tri_state_buffer_4bit_1_o_2), .D_3(tri_state_buffer_4bit_1_o_3),
    .Q_0(decoder_6_to_64_1_p19), .Q_1(decoder_6_to_64_1_p10), .Q_2(decoder_6_to_64_1_p9),
    .Q_3(decoder_6_to_64_1_p8));
  counter_resetable counter_resetable_2 (
    .C(pc_inc), .R(1'b0), .S(1'b0), .D_0(1'b0), .D_1(1'b0), .D_2(1'b0), .D_3(1'b0), .R_a(pc_reset),
    .O_0(counter_resetable_2_o_0), .O_1(counter_resetable_2_o_1), .O_2(counter_resetable_2_o_2),
    .O_3(counter_resetable_2_o_3));
  tri_state_buffer_4bit tri_state_buffer_4bit_3 (
    .D_0(counter_resetable_2_o_0), .D_1(counter_resetable_2_o_1), .D_2(counter_resetable_2_o_2),
    .D_3(counter_resetable_2_o_3), .E(pc_out), .O_0(tri_state_buffer_4bit_1_o_0),
    .O_1(tri_state_buffer_4bit_1_o_1), .O_2(tri_state_buffer_4bit_1_o_2), .O_3(tri_state_buffer_4bit_1_o_3));
  register_simple register_simple_1 (
    .E_out(reg_A_in), .CLK(and_2_out), .D_0(tri_state_buffer_4bit_1_o_0), .D_1(tri_state_buffer_4bit_1_o_1),
    .D_2(tri_state_buffer_4bit_1_o_2), .D_3(tri_state_buffer_4bit_1_o_3), .Q_0(register_simple_1_q_0),
    .Q_1(register_simple_1_q_1), .Q_2(register_simple_1_q_2), .Q_3(register_simple_1_q_3));
  register_simple register_simple_2 (
    .E_out(in_4), .CLK(and_2_out), .D_0(tri_state_buffer_4bit_1_o_0), .D_1(tri_state_buffer_4bit_1_o_1),
    .D_2(tri_state_buffer_4bit_1_o_2), .D_3(tri_state_buffer_4bit_1_o_3), .Q_0(register_simple_2_q_0),
    .Q_1(register_simple_2_q_1), .Q_2(register_simple_2_q_2), .Q_3(register_simple_2_q_3));
  tri_state_buffer_4bit tri_state_buffer_4bit_4 (
    .D_0(adder_2_p10), .D_1(adder_2_p11), .D_2(adder_2_p12), .D_3(adder_2_p13), .E(in_6),
    .O_0(tri_state_buffer_4bit_1_o_0), .O_1(tri_state_buffer_4bit_1_o_1), .O_2(tri_state_buffer_4bit_1_o_2),
    .O_3(tri_state_buffer_4bit_1_o_3));
  tri_state_buffer_4bit tri_state_buffer_4bit_5 (
    .D_0(register_simple_1_q_0), .D_1(register_simple_1_q_1), .D_2(register_simple_1_q_2),
    .D_3(register_simple_1_q_3), .E(in_2), .O_0(tri_state_buffer_4bit_1_o_0),
    .O_1(tri_state_buffer_4bit_1_o_1), .O_2(tri_state_buffer_4bit_1_o_2), .O_3(tri_state_buffer_4bit_1_o_3));
  tri_state_buffer_4bit tri_state_buffer_4bit_6 (
    .D_0(register_simple_2_q_0), .D_1(register_simple_2_q_1), .D_2(register_simple_2_q_2),
    .D_3(register_simple_2_q_3), .E(in_3), .O_0(tri_state_buffer_4bit_1_o_0),
    .O_1(tri_state_buffer_4bit_1_o_1), .O_2(tri_state_buffer_4bit_1_o_2), .O_3(tri_state_buffer_4bit_1_o_3));
  // adder adder_2: pin names not known; wires that end beside it: in_5, register_simple_1_q_0, register_simple_1_q_1, register_simple_1_q_2, register_simple_1_q_3, register_simple_2_q_0, register_simple_2_q_1, register_simple_2_q_2, register_simple_2_q_3, adder_2_p10, adder_2_p11, adder_2_p12, adder_2_p13

  // Notes on the sheet:
  //   clk: Hz: 50000
endmodule
